# Fritzing sketch sketch_03.05_imu_external_power_marcell (saved by Fritzing 0.9.3b)
breadboards: 1

parts:
  WeMos_D1_Mini1 = WeMos D1 Mini
  R1 = Resistor [tolerance=±5% resistance=10k package="2512 [SMD]"]
  Q1 = MOSFET-NCHANNEL [package=to-92]
  M1 = DC Motor
  Part1 = InvenSense MPU6050
  VCC1 = 4 x AAA Battery Mount
  D1 = Zener Diode [part_number=1N4732A breakdown_voltage=3.6V package="300 mil [THT]"]
  R2 = Resistor [tolerance=±5% resistance=100 package=THT]
  R3 = Rotary Potentiometer (Small) [maximum_resistance=10kΩ package=THT]

nets:
  5V: WeMos_D1_Mini1.5V, Part1.VCC, R3.leg1
  N1: WeMos_D1_Mini1.A0, R3.wiper
  N2: WeMos_D1_Mini1.D1, Part1.SCL
  N3: WeMos_D1_Mini1.D2, Part1.SDA
  N4: WeMos_D1_Mini1.D5, R2.Pin_0
  N5: WeMos_D1_Mini1.G, R1.Pin_1, Q1.G, Part1.GND, VCC1.-, R3.leg2
  N6: R1.Pin_0, Q1.S, R2.Pin_1
  N7: Q1.D, M1.pin_2, D1.anode
  N8: M1.pin_1, VCC1.+, D1.cathode

notes:
  Arm to control
  1024
  10
